# Fritzing sketch FlameSensor (saved by Fritzing 0.9.9b)
breadboards: 1

parts:
  Part1 = KY-026 Flame Sensor Module [package="Breakout board"]
  Part2 = Arduino Nano (Rev3.0)
  LED1 = LED - 5mm [color="Red (633nm)" current=0.030 package="5 mm [THT]"]
  R1 = Resistor [tolerance=±5% power=0.25 resistance=220 package=THT]
  J1 = Piezo Speaker

nets:
  N1: Part1.G, Part2.GND, R1.Pin_0, J1.pin1
  N2: Part1.+, Part2.5V
  N3: Part1.D0, Part2.D7
  N4: Part2.D9, LED1.anode
  N5: Part2.D12/MISO, J1.pin2
  N6: LED1.cathode, R1.Pin_1

custom parts:
  KY-026 Flame Sensor Module: KEYES KY-026 Arduino Flame Sensor Module reacts iin the presence of fire.
